# Fritzing sketch LEDStrip (saved by Fritzing 0.9.4)
breadboards: 1

parts:
  12V_Input = Power plug
  LED_Strip = female pin header, 4 pins [form="♀ (female)"]
  WeMos_D1_Mini1 = WeMos D1 Mini
  Step_down_Regulator = female pin header, 3 pins [form="♀ (female)"]
  Action_Btn = Pushbutton [package="[SMD]"]
  MSGWEQ7 = MSGEQ7 [package=soic8]
  1N4007 = Rectifier Diode [part_number=1N4001 package="Melf DO-213 AB [SMD]"]
  MOSFET = MOSFET-NCHANNEL [package=sot23-3]
  MOSFET_2 = MOSFET-NCHANNEL [package=sot23-3]
  MOSFET_3 = MOSFET-NCHANNEL [package=sot23-3]
  10nF = Ceramic Capacitor [capacitance=10nF package="0603 [SMD, multilayer]"]
  100nF = Ceramic Capacitor [capacitance=100nF package="0603 [SMD, multilayer]"]
  33pF = Ceramic Capacitor [capacitance=33pF package="0603 [SMD, multilayer]"]
  100nF_2 = Ceramic Capacitor [capacitance=100nF package="0603 [SMD, multilayer]"]
  1kΩ = Resistor [tolerance=±5% resistance=1k package="0603 [SMD]"]
  91Ω = Resistor [tolerance=±5% resistance=91 package="0603 [SMD]"]
  LED1 = smd LED [color="Blue (430nm)" package="0603 [SMD]"]
  MOSFET1 = MOSFET-NCHANNEL [package=sot23-3]
  MOSFET2 = MOSFET-NCHANNEL [package=sot23-3]
  MOSFET3 = MOSFET-NCHANNEL [package=sot23-3]
  LED_Strip1 = female pin header, 4 pins [form="♀ (female)"]
  220kΩ = Resistor [tolerance=±5% resistance=220k package="0603 [SMD]"]
  LED_Strip2 = female pin header, 5 pins [form="♀ (female)"]

nets:
  GND: 12V_Input.GND, WeMos_D1_Mini1.G, Step_down_Regulator.pin2, MSGWEQ7.GND, MOSFET.S, MOSFET_2.S, MOSFET_3.S, 100nF.1, 33pF.0, 100nF_2.1, 1kΩ.Pin_1, 91Ω.Pin_1, MOSFET1.S, MOSFET2.S, MOSFET3.S, LED_Strip2.pin5
  N1: 12V_Input.VCC, LED_Strip.pin4, 1N4007.anode, LED_Strip1.pin4
  N2: LED_Strip.pin1, MOSFET.D
  N3: LED_Strip.pin2, MOSFET_2.D
  N4: LED_Strip.pin3, MOSFET_3.D
  5V: WeMos_D1_Mini1.5V, Step_down_Regulator.pin3, Action_Btn.Pin_1, Action_Btn.Pin_2, MSGWEQ7.VDD, 100nF_2.0, 220kΩ.Pin_1, LED_Strip2.pin4
  N5: WeMos_D1_Mini1.A0, MSGWEQ7.DCOUT
  N6: WeMos_D1_Mini1.D0, MOSFET_3.G
  N7: WeMos_D1_Mini1.D1, MOSFET_2.G
  N8: WeMos_D1_Mini1.D2, MOSFET.G
  N9: WeMos_D1_Mini1.D3, MOSFET3.G
  N10: WeMos_D1_Mini1.D4, MSGWEQ7.RESET
  N11: WeMos_D1_Mini1.D5, Action_Btn.Pin_3, Action_Btn.Pin_4, 1kΩ.Pin_0
  N12: WeMos_D1_Mini1.D6, LED1.anode
  N13: WeMos_D1_Mini1.D7, MOSFET1.G
  N14: WeMos_D1_Mini1.D8, MOSFET2.D
  N15: WeMos_D1_Mini1.TX, MSGWEQ7.STROBE
  N16: Step_down_Regulator.pin1, 1N4007.cathode
  N17: MSGWEQ7.AUDIO_IN, 10nF.0
  N18: MSGWEQ7.CG, 100nF.0
  N19: MSGWEQ7.CKIN, 33pF.1, 220kΩ.Pin_0
  N20: 10nF.1, LED_Strip2.pin2
  N21: 91Ω.Pin_0, LED1.cathode
  N22: MOSFET1.D, LED_Strip1.pin1
  N23: MOSFET2.G, LED_Strip1.pin2
  N24: MOSFET3.D, LED_Strip1.pin3

notes:
  B R G P
