# Fritzing sketch LEDStrip (saved by Fritzing 0.9.4)
circuit board: 9.46116cm x 6.43019cm
breadboards: 2

parts:
  12V_Input = Power plug
  LED_Addr = female pin header, 3 pins [form="♀ (female)"]
  5v = female pin header, 2 pins [form="♀ (female)"]
  Schottky = Rectifier Diode [package="Melf DO-213 AA [SMD]"]
  33uH = Inductors [package=cr54]
  Mic = female pin header, 5 pins [form="♀ (female)"]
  Schottky_2 = Rectifier Diode [package="Melf DO-213 AA [SMD]"]
  33uH_2 = Inductors [package=cr54]
  Out = female pin header, 2 pins [form="♀ (female)"]
  12V_Out = female pin header, 2 pins [form="♀ (female)"]
  MSGEQ1 = MSGEQ7 [chip_label=IC package="DIP (Dual Inline) [THT]"]
  LM2596 = LM2596 [package=q5-dd_spx29300]
  33pF = Capacitor [package=0603-cap]
  100nF = Capacitor [package=0603-cap]
  10nF = Capacitor [package=0603-cap]
  100nF_2 = Capacitor [package=0603-cap]
  LED_Strip = female pin header, 4 pins [form="♀ (female)"]
  LED_Matrix = female pin header, 5 pins [form="♀ (female)"]
  Pot_BK = female pin header, 3 pins [form="♀ (female)"]
  Gain_Pot = female pin header, 3 pins [form="♀ (female)"]
  Button = female pin header, 4 pins [form="♀ (female)"]
  220Ω = Resistor [tolerance=±5% resistance=220 package="0603 [SMD]"]
  2kΩ = Resistor [tolerance=±1% resistance=2k package="0603 [SMD]"]
  1kΩ = Resistor [tolerance=±1% resistance=1k package="0603 [SMD]"]
  200kΩ = Resistor [tolerance=±1% resistance=200k package="0603 [SMD]"]
  20kΩ = Resistor [tolerance=±1% resistance=20k package="0603 [SMD]"]
  330Ω = Resistor [tolerance=±1% resistance=330 package="0603 [SMD]"]
  MOSFET_G = Basic FET N-Channel [package="D2Pak [SMD]"]
  MOSFET_R = Basic FET N-Channel [package="D2Pak [SMD]"]
  MOSFET_B = Basic FET N-Channel [package="D2Pak [SMD]"]
  LM2596_2 = LM2596 [package=q5-dd_spx29300]
  330µF = Tantalum Capacitor [capacitance=330µF voltage=16V package="D 7343 [SMD, tantalum]"]
  330µF_2 = Tantalum Capacitor [capacitance=330µF voltage=16V package="D 7343 [SMD, tantalum]"]
  220µF = Tantalum Capacitor [capacitance=220µF voltage=16V package="D 7343 [SMD, tantalum]"]
  220µF_2 = Tantalum Capacitor [capacitance=220µF package="B 3528 [SMD, tantalum]"]
  220µF_3 = Tantalum Capacitor [capacitance=220µF package="B 3528 [SMD, tantalum]"]
  ESP32_Header = female pin header, 22 pins [form="♀ (female)"]
  ESP32_Header_2 = female pin header, 22 pins [form="♀ (female)"]
  Backlight = JUMPER-3 [package=sj_3]
  Gain = JUMPER-3 [package=sj_3]
  TFT = female pin header, 8 pins [form="♀ (female)"]
  LCD = female pin header, 4 pins [form="♀ (female)"]
  ESP32_S3_Dev_Board = ESP32-S2-DevKitC-1 [part_number=ESP32-S2-DevKitC-1]

nets:
  GND: 12V_Input.GND, LED_Addr.pin3, 5v.pin1, Schottky.anode, Mic.pin5, Schottky_2.anode, Out.pin1, 12V_Out.pin1, MSGEQ1.VSS, LM2596.GND, LM2596.On/Off, 33pF.2, 100nF.1, 100nF_2.1, LED_Matrix.pin4, Pot_BK.pin1, Gain_Pot.pin1, 220Ω.Pin_0, 1kΩ.Pin_1, MOSFET_G.source, MOSFET_R.source, MOSFET_B.source, LM2596_2.GND, LM2596_2.On/Off, 330µF.-, 330µF_2.-, 220µF.-, 220µF_2.-, 220µF_3.-, ESP32_Header_2.pin22, Backlight.1, Gain.1, TFT.pin8, LCD.pin1, ESP32_S3_Dev_Board.pin_22, ESP32_S3_Dev_Board.pin_23, ESP32_S3_Dev_Board.pin_44
  VIN: 12V_Input.VCC, 12V_Out.pin2, LM2596.VIN, LED_Strip.pin4, LM2596_2.VIN, 330µF.+, 330µF_2.+, 220µF.+
  N1: LED_Addr.pin1, 5v.pin2, 33uH_2.2, LM2596.Feedback, LED_Matrix.pin5, 220µF_2.+
  N2: LED_Addr.pin2, 330Ω.Pin_1
  N3: Schottky.cathode, 33uH.1, LM2596_2.OUT
  N4: 33uH.2, MSGEQ1.VDD, 100nF_2.2, 200kΩ.Pin_0, LM2596_2.Feedback, 220µF_3.+, ESP32_Header.pin2, ESP32_S3_Dev_Board.pin_21
  N5: Mic.pin2, 20kΩ.Pin_1
  N6: Mic.pin3, Gain_Pot.pin2, Gain.2
  N7: Mic.pin4, Out.pin2, Pot_BK.pin3, Gain_Pot.pin3, Button.pin2, Button.pin3, ESP32_Header.pin22, Backlight.3, Gain.3, TFT.pin7, LCD.pin2, ESP32_S3_Dev_Board.pin_1, ESP32_S3_Dev_Board.pin_2
  N8: Schottky_2.cathode, 33uH_2.1, LM2596.OUT
  N9: MSGEQ1.OUT, ESP32_Header_2.pin19, ESP32_S3_Dev_Board.pin_41
  N10: MSGEQ1.STROBE, ESP32_Header_2.pin18, ESP32_S3_Dev_Board.pin_40
  N11: MSGEQ1.IN, 10nF.1
  N12: MSGEQ1.pin6, 100nF.2
  N13: MSGEQ1.GND, ESP32_Header.pin18, ESP32_S3_Dev_Board.pin_5
  N14: MSGEQ1.CKIN, 33pF.1, 200kΩ.Pin_1
  N15: 10nF.2, 2kΩ.Pin_0
  N16: LED_Strip.pin1, MOSFET_B.drain
  N17: LED_Strip.pin2, MOSFET_R.drain
  N18: LED_Strip.pin3, MOSFET_G.drain
  N19: LED_Matrix.pin1, ESP32_Header_2.pin7, ESP32_S3_Dev_Board.pin_29
  N20: LED_Matrix.pin2, ESP32_Header_2.pin6, ESP32_S3_Dev_Board.pin_28
  N21: LED_Matrix.pin3, ESP32_Header_2.pin8, ESP32_S3_Dev_Board.pin_30
  N22: Pot_BK.pin2, Backlight.2, TFT.pin1
  N23: Button.pin1, 1kΩ.Pin_0, ESP32_Header.pin19, ESP32_S3_Dev_Board.pin_4
  N24: Button.pin4, 220Ω.Pin_1
  N25: 2kΩ.Pin_1, 20kΩ.Pin_0
  N26: 330Ω.Pin_0, ESP32_Header_2.pin17, ESP32_S3_Dev_Board.pin_39
  N27: MOSFET_G.Gate, ESP32_Header_2.pin16, ESP32_S3_Dev_Board.pin_38
  N28: MOSFET_R.Gate, ESP32_Header_2.pin15, ESP32_S3_Dev_Board.pin_37
  N29: MOSFET_B.Gate, ESP32_Header_2.pin14, ESP32_S3_Dev_Board.pin_36
  N30: ESP32_Header.pin3, TFT.pin2, ESP32_S3_Dev_Board.pin_20
  N31: ESP32_Header.pin4, TFT.pin3, ESP32_S3_Dev_Board.pin_19
  N32: ESP32_Header.pin5, TFT.pin4, ESP32_S3_Dev_Board.pin_18
  N33: ESP32_Header.pin6, TFT.pin6, ESP32_S3_Dev_Board.pin_17
  N34: ESP32_Header.pin7, TFT.pin5, ESP32_S3_Dev_Board.pin_16
  N35: ESP32_Header.pin8, LCD.pin3, ESP32_S3_Dev_Board.pin_15
  N36: ESP32_Header.pin12, LCD.pin4, ESP32_S3_Dev_Board.pin_11

notes:
  Note that the ESP32 board below is ESP32 S2. I'm actually using ESP32 S3 so I'm keeping the pin LOCATION constant and ignoring the pin NUMBERS for the bottom rail which differ between S2 and S3.
  GND RNG RSH TSH TIP
  3.3V    GND
  GND
  GND   GND
  3.3V   3.3V
  MSGEQ7 Reset
  1
  8
  GND   VPP   Gain   Out   AR
  MSGEQ7 Out
  MSGEQ7 In
  MGEQ7 Stobe
  MGEQ7 CLK
  GND    12V
  BKL    CS    DC    RES   SDA   SCL   VCC   GND
  SDA   SCK   VDD   GND
  12V  Green  Red  Blue
  5V    GND
  3.3V GND
  3.3V   Out   GND

custom parts:
  MSGEQ7: A DIP stand-in part for whatever IC you want. With 8 pins on a 300mil dual inline package (DIP) footprint.
  LM2596: LM2596 SIMPLE SWITCHER® Power Converter 150-kHz 3-A Step-Down Voltage Regulator
  ESP32-S2-DevKitC-1: ESP32-S2-DevKitC-1 is an entry-level development board based on ESP32-S2-SOLO (on-board PCB antenna). It is based on the ESP32 microcontroller that boasts Wifi, Bluetooth, Ethernet and Low Power support all in a single chip. (vanepp) Feb 2022: converted to ESP32-S2-DevKitC-1. This module is 44pins long (2x22) and 11 pins width.
